# Fritzing sketch LED (saved by Fritzing 0.9.6b)
breadboards: 1

parts:
  VCC1 = Battery block 9V
  R1 = Resistor [tolerance=±5% resistance=220 package="2512 [SMD]"]
  LED1 = LED - 3mm [color="Red (633nm)" current=0.030 package="3 mm [THT]"]
  S1 = Pushbutton [package="[THT]"]

nets:
  N1: VCC1.-, LED1.anode
  N2: VCC1.+, S1.Pin_3, S1.Pin_4
  N3: R1.Pin_0, S1.Pin_1, S1.Pin_2
  N4: R1.Pin_1, LED1.cathode
